// Logisim project 8bit_CPU.circ as structural Verilog: 2 circuits, main circuit main
module main (
  input  in_1,
  input  in_2,
  input  in_3,
  input  in_4,
  input  in_5,
  input  in_6,
  input  in_7,
  input  in_8,
  input  in_9,
  input  in_10,
  input  in_11,
  input  in_12,
  input  in_13,
  input  in_14,
  input  in_15,
  input  in_16,
  input  in_17,
  input  in_18,
  input  in_19,
  input  in_20,
  input  in_21,
  input  in_22,
  input  in_23,
  input  in_24,
  input  in_25,
  input  in_26,
  input  in_27,
  input  in_28,
  input  in_29,
  input  in_30,
  input  in_31,
  input  in_32,
  input  in_33,
  input  in_34,
  input  in_35,
  input  in_36,
  input  in_37,
  input  in_38,
  input  in_39,
  input  in_40,
  input  in_41,
  input  in_42,
  output [7:0] D0_7pins
);

  wire ACR, adder_1_cout, adder_2_cout, and_1_out, and_3_out, bitselector_1_out, CL1, CL2, D_IR, or_1_out,
       or_2_out, or_5_out, or_6_out, pull_resistor_1_node, pull_resistor_3_node, pull_resistor_4_node;
  wire [2:0] bit_extender_1_out, counter_1_q;
  wire [6:0] controlled_buffer_24_out;
  wire [7:0] ADD_q, adder_1_out, adder_2_out, adder_3_out, AI_q, and_2_out, BI_q, bit_extender_2_out,
       controlled_buffer_2_out, controlled_buffer_3_out, controlled_buffer_6_out, controlled_buffer_9_out,
       controlled_buffer_14_out, controlled_buffer_19_out, controlled_buffer_26_out,
       controlled_buffer_29_out, DL_q, DOR_q, not_2_out, or_3_out, PCH_q, PCHS_q, PCL_q, PCLS_q, PD_q,
       pull_resistor_2_node, S_q, shifter_1_out, undriven, xor_1_out;
  wire [7:7] controlled_buffer_25_out;
  wire [15:0] ADB;

  Clock clock_1 (.out(CL1));
  Register IR (.D(PD_q), .en(D_IR), .clk(CL1), .clr(in_1));  // open: Q
  ROM #(.addrWidth(11), .dataWidth(64)) rom_1 ();  // open: addr, data
  not not_1 (CL2, CL1);
  Counter #(.max('h7), .width(3)) counter_1 (
    .clr(in_1), .up(1'b1), .count(1'b1), .clk(CL2), .Q(counter_1_q));  // open: load, D, carry
  Register PD (.D(D0_7pins), .en(CL2), .clk(CL2), .Q(PD_q), .clr(in_1));
  Decoder #(.enable("false"), .select(3)) decoder_1 (.sel(counter_1_q));  // open: out0, out1, out2, out3, out4, out5, out6, out7
  RAM #(.addrWidth(16), .enables("line")) ram_1 (.addr(ADB), .we(in_14), .clk(CL1), .din(D0_7pins), .dout(D0_7pins));
  Register DOR (.D(controlled_buffer_2_out), .en(CL1), .clk(CL1), .Q(DOR_q), .clr(in_1));
  assign D0_7pins = in_14 ? DOR_q : 8'bz;  // Controlled_Buffer controlled_buffer_1
  assign controlled_buffer_2_out = in_2 ? undriven : 8'bz;  // Controlled_Buffer controlled_buffer_2
  assign not_2_out = ~controlled_buffer_2_out;  // NOT_Gate not_2, 8 bits wide
  assign controlled_buffer_3_out = in_27 ? not_2_out : 8'bz;  // Controlled_Buffer controlled_buffer_3
  and and_1 (and_1_out, in_33, adder_1_cout);
  assign controlled_buffer_2_out = in_12 ? PCL_q : 8'bz;  // Controlled_Buffer controlled_buffer_4
  assign controlled_buffer_3_out = in_28 ? controlled_buffer_2_out : 8'bz;  // Controlled_Buffer controlled_buffer_5
  Adder adder_1 (.a(BI_q), .b(AI_q), .out(adder_1_out), .cin(in_30), .cout(adder_1_cout));
  assign bit_extender_1_out = {{2{1'b0}}, 1'b1};  // Bit_Extender bit_extender_1
  Register AI (.D(controlled_buffer_19_out), .en(or_5_out), .clk(CL1), .Q(AI_q), .clr(in_1));
  Register DL (.D(D0_7pins), .en(CL2), .clk(CL2), .Q(DL_q), .clr(in_1));
  or or_1 (or_1_out, in_10, in_9);
  assign controlled_buffer_6_out = in_9 ? PCL_q : 8'bz;  // Controlled_Buffer controlled_buffer_6
  or or_2 (or_2_out, in_27, in_28, in_29);
  BitSelector bitselector_1 (.in(AI_q), .out(bitselector_1_out), .sel(3'b000));
  assign controlled_buffer_6_out = in_10 ? controlled_buffer_14_out : 8'bz;  // Controlled_Buffer controlled_buffer_7
  Register PCLS (.D(controlled_buffer_6_out), .en(or_1_out), .clk(CL1), .Q(PCLS_q), .clr(in_1));
  assign bit_extender_2_out = {{7{1'b0}}, in_11};  // Bit_Extender bit_extender_2
  Register PCL (.D(adder_2_out), .en(CL2), .clk(CL2), .Q(PCL_q), .clr(in_1));
  assign controlled_buffer_3_out = in_29 ? controlled_buffer_14_out : 8'bz;  // Controlled_Buffer controlled_buffer_8
  Register BI (.D(controlled_buffer_3_out), .en(or_2_out), .clk(CL1), .Q(BI_q), .clr(in_1));
  assign controlled_buffer_9_out = in_33 ? adder_1_out : 8'bz;  // Controlled_Buffer controlled_buffer_9
  assign and_2_out = BI_q & AI_q;  // AND_Gate and_2, 8 bits wide
  assign controlled_buffer_9_out = in_34 ? and_2_out : 8'bz;  // Controlled_Buffer controlled_buffer_10
  assign xor_1_out = BI_q ^ AI_q;  // XOR_Gate xor_1, 8 bits wide
  assign controlled_buffer_9_out = in_35 ? xor_1_out : 8'bz;  // Controlled_Buffer controlled_buffer_11
  assign or_3_out = BI_q | AI_q;  // OR_Gate or_3, 8 bits wide
  assign controlled_buffer_9_out = in_36 ? or_3_out : 8'bz;  // Controlled_Buffer controlled_buffer_12
  assign controlled_buffer_9_out = in_37 ? shifter_1_out : 8'bz;  // Controlled_Buffer controlled_buffer_13
  Shifter #(.shift("lr")) shifter_1 (.in(AI_q), .\dist (bit_extender_1_out), .out(shifter_1_out));
  and and_3 (and_3_out, bitselector_1_out, in_37);
  or or_4 (ACR, and_1_out, and_3_out);
  Adder adder_2 (.a(PCLS_q), .b(bit_extender_2_out), .out(adder_2_out), .cout(adder_2_cout));  // open: cin
  assign controlled_buffer_14_out[0] = in_21 ? pull_resistor_1_node : 1'bz;  // Controlled_Buffer controlled_buffer_14
  assign controlled_buffer_14_out[1] = in_22 ? pull_resistor_1_node : 1'bz;  // Controlled_Buffer controlled_buffer_15
  assign controlled_buffer_14_out[2] = in_23 ? pull_resistor_1_node : 1'bz;  // Controlled_Buffer controlled_buffer_16
  Pull_Resistor pull_resistor_1 (.node(pull_resistor_1_node));
  assign controlled_buffer_14_out = in_3 ? DL_q : 8'bz;  // Controlled_Buffer controlled_buffer_17
  assign controlled_buffer_14_out = in_13 ? PCL_q : 8'bz;  // Controlled_Buffer controlled_buffer_18
  Register ADD (.D(controlled_buffer_9_out), .en(CL2), .clk(CL2), .Q(ADD_q));  // open: clr
  Pull_Resistor pull_resistor_2 (.node(pull_resistor_2_node));
  or or_5 (or_5_out, in_41, in_42);
  assign controlled_buffer_19_out = in_41 ? pull_resistor_2_node : 8'bz;  // Controlled_Buffer controlled_buffer_19
  assign controlled_buffer_14_out = in_38 ? ADD_q : 8'bz;  // Controlled_Buffer controlled_buffer_20
  assign controlled_buffer_19_out = in_42 ? {controlled_buffer_25_out[7], controlled_buffer_24_out} : 8'bz;  // Controlled_Buffer controlled_buffer_21
  or or_6 (or_6_out, in_16, in_15);
  assign controlled_buffer_2_out = in_12 ? PCH_q : 8'bz;  // Controlled_Buffer controlled_buffer_22
  assign controlled_buffer_14_out = in_24 ? S_q : 8'bz;  // Controlled_Buffer controlled_buffer_23
  assign controlled_buffer_24_out = in_39 ? ADD_q[6:0] : 7'bz;  // Controlled_Buffer controlled_buffer_24
  assign controlled_buffer_25_out[7] = in_40 ? ADD_q[7] : 1'bz;  // Controlled_Buffer controlled_buffer_25
  assign controlled_buffer_26_out = in_16 ? {{7{controlled_buffer_29_out[7]}}, controlled_buffer_29_out[0]} : 8'bz;  // Controlled_Buffer controlled_buffer_26
  assign controlled_buffer_26_out = in_15 ? PCH_q : 8'bz;  // Controlled_Buffer controlled_buffer_27
  Register PCHS (.D(controlled_buffer_26_out), .en(or_6_out), .clk(CL1), .Q(PCHS_q), .clr(in_1));
  Register PCH (.D(adder_3_out), .en(CL2), .clk(CL2), .Q(PCH_q), .clr(in_1));
  assign controlled_buffer_2_out = in_20 ? {controlled_buffer_25_out[7], controlled_buffer_24_out} : 8'bz;  // Controlled_Buffer controlled_buffer_28
  Register S (.D({controlled_buffer_25_out[7], controlled_buffer_24_out}), .en(in_25), .clk(CL1), .Q(S_q), .clr(in_1));
  Adder adder_3 (.a(PCHS_q), .b({8{1'b0}}), .out(adder_3_out), .cin(adder_2_cout));  // open: cout
  assign {{7{controlled_buffer_29_out[7]}}, controlled_buffer_29_out[0]} = in_4 ? undriven : 8'bz;  // Controlled_Buffer controlled_buffer_29
  assign {{7{controlled_buffer_29_out[7]}}, controlled_buffer_29_out[0]} = in_18 ? PCH_q : 8'bz;  // Controlled_Buffer controlled_buffer_30
  assign {{7{controlled_buffer_29_out[7]}}, controlled_buffer_29_out[0]} = in_19 ? {controlled_buffer_25_out[7], controlled_buffer_24_out} : 8'bz;  // Controlled_Buffer controlled_buffer_31
  assign {controlled_buffer_25_out[7], controlled_buffer_24_out} = in_26 ? S_q : 8'bz;  // Controlled_Buffer controlled_buffer_32
  Register ABH (
    .D({{7{controlled_buffer_29_out[7]}}, controlled_buffer_29_out[0]}), .en(in_7), .clk(CL1), .Q(ADB[15:8]),
    .clr(in_1));
  Register ABL (.D(controlled_buffer_14_out), .en(in_8), .clk(CL1), .Q(ADB[7:0]), .clr(in_1));
  Pull_Resistor pull_resistor_3 (.node(pull_resistor_3_node));
  assign controlled_buffer_29_out[0] = in_5 ? pull_resistor_3_node : 1'bz;  // Controlled_Buffer controlled_buffer_33
  Pull_Resistor pull_resistor_4 (.node(pull_resistor_4_node));
  assign controlled_buffer_29_out[7] = in_6 ? pull_resistor_4_node : 1'bz;  // Controlled_Buffer controlled_buffer_34

  // Other names for the same wires on the sheet: ADD_ADL = in_38; ADD_SB06 = in_39; ADD_SB7 = in_40; ADH_ABH = in_7;
  //   ADH_PCH = in_16; ADL_ABL = in_8; ADL_ADD = in_29; ADL_PCL = in_10; ANDS = in_34; DB_ADD = in_28;
  //   DBx_ADD = in_27; DDA = in_31; DL_ADH = in_4; DL_ADL = in_3; DL_DB = in_2; DSA = in_32; EORS = in_35;
  //   I_ADDC = in_30; I_PC = in_11; O_ADD = in_41; O_ADH0 = in_5; O_ADH17 = in_6; O_ADL0 = in_21; O_ADL1 = in_22;
  //   O_ADL2 = in_23; ORS = in_36; PCH_ADH = in_18; PCH_DB = in_17; PCH_PCH = in_15; PCL_ADL = in_13; PCL_DB = in_12;
  //   PCL_PCL = in_9; RST = in_1; RW = in_14; S_ADL = in_24; S_SB = in_26; SB_ADD = in_42; SB_ADH = in_19;
  //   SB_DB = in_20; SB_S = in_25; SRS = in_37; SUMS = in_33
endmodule

module ALU (
  input  [7:0] RegA,
  input  [7:0] RegB,
  input  Su,
  output [7:0] out_4
);

  wire adder_1_cout;
  wire [7:0] bit_extender_1_out, xor_1_out;

  assign bit_extender_1_out = {{7{Su}}, Su};  // Bit_Extender bit_extender_1
  assign xor_1_out = RegB ^ bit_extender_1_out;  // XOR_Gate xor_1, 8 bits wide
  Adder adder_1 (.a(RegA), .b(xor_1_out), .out(out_4), .cin(Su), .cout(adder_1_cout));
endmodule
